# Fritzing sketch CS207 - Final Project (saved by Fritzing 0.9.5d)
breadboards: 1

parts:
  Part1 = Arduino Uno (Rev3) - ICSP
  R1 = Resistor [tolerance=±5% resistance=220 package=THT]
  R2 = Resistor [tolerance=±5% resistance=220 package=THT]
  R3 = Resistor [tolerance=±5% resistance=220 package=THT]
  LED1 = RGB LED (com. anode, rbg) [package="5 mm [THT]"]
  R5 = Resistor [tolerance=±5% resistance=560 package=THT]
  R6 = Resistor [tolerance=±5% resistance=560 package=THT]
  R7 = Resistor [tolerance=±5% resistance=560 package=THT]
  R8 = Resistor [tolerance=±5% resistance=560 package=THT]
  R9 = Resistor [tolerance=±5% resistance=560 package=THT]
  R10 = Resistor [tolerance=±5% resistance=560 package=THT]
  R11 = Resistor [tolerance=±5% resistance=560 package=THT]
  R12 = Resistor [tolerance=±5% resistance=560 package=THT]
  R13 = Resistor [tolerance=±5% resistance=560 package=THT]
  R14 = Resistor [tolerance=±5% resistance=560 package=THT]
  R15 = Resistor [tolerance=±5% resistance=560 package=THT]
  R16 = Resistor [tolerance=±5% resistance=560 package=THT]
  J1 = Piezo Speaker

nets:
  N1: Part1.ICSP_MOSI, Part1.D11_PWM/MOSI, R3.Pin_1
  N2: Part1.D9_PWM, R1.Pin_1
  N3: Part1.D10_PWM/SS, R2.Pin_1
  N4: Part1.GND, LED1.common_anode, J1.pin2
  N5: Part1.D0/RX, R6.Pin_0
  N6: Part1.D1/TX, R7.Pin_0
  N7: Part1.D2, R8.Pin_0
  N8: Part1.D3_PWM, R9.Pin_0
  N9: R1.Pin_0, LED1.red_cathode
  N10: R2.Pin_0, LED1.blue_cathode
  N11: R3.Pin_0, LED1.green_cathode
  N12: R5.Pin_0, R10.Pin_0, R14.Pin_0
  N13: R6.Pin_1, R10.Pin_1
  N14: R7.Pin_1, R11.Pin_1
  N15: R8.Pin_1, R12.Pin_1
  N16: R9.Pin_1, R13.Pin_1
  N17: R11.Pin_0, R14.Pin_1, R15.Pin_0
  N18: R12.Pin_0, R15.Pin_1, R16.Pin_0
  N19: R13.Pin_0, R16.Pin_1, J1.pin1
